# Fritzing sketch Blink (saved by Fritzing 0.9.8b)
breadboards: 1

parts:
  Part1 = Arduino Uno (Rev3)
  LED1 = LED - 5mm [color="Red (633nm)" current=0.030 package="5 mm [THT]"]
  R1 = Resistor [tolerance=±5% power=0.25 resistance=330 package=THT]

nets:
  N1: Part1.D6_PWM, LED1.anode
  N2: Part1.GND, R1.Pin_1
  N3: LED1.cathode, R1.Pin_0
